// Logisim project ex1.circ as structural Verilog
module Exp1 (
  input  A0,
  input  B0,
  output SOMA,
  output CARRY_OUT
);

  xor xor_1 (SOMA, A0, B0);
  and and_1 (CARRY_OUT, A0, B0);
endmodule

module somadorCompleto (
  input  A,
  input  B,
  input  _0,
  output out_4,
  output out_5
);

  wire exp1_1_carry_out, exp1_1_soma, exp1_2_carry_out;

  Exp1 exp1_1 (.A0(A), .B0(B), .SOMA(exp1_1_soma), .CARRY_OUT(exp1_1_carry_out));
  Exp1 exp1_2 (.A0(exp1_1_soma), .B0(_0), .SOMA(out_4), .CARRY_OUT(exp1_2_carry_out));
  or or_1 (out_5, exp1_2_carry_out, exp1_1_carry_out);

  // Notes on the sheet:
  //   C
  //   0
  //   0
endmodule
